# Fritzing sketch breaboard (saved by Fritzing 0.9.2b)
circuit board: 8.46667cm x 5.64444cm
breadboards: 4

parts:
  VCC1 = Battery
  VCC2 = Battery
  U1 = DC-DC_CONVERTER [package=dc-dc_converter]
  Q1 = NPN-Transistor [package="TO92 [THT]"]
  M1 = DC Motor
  M2 = DC Motor
  MBED1 = mbed
  Q2 = NPN-Transistor [package="TO92 [THT]"]
  Part1 = BH1750FVI Breakout Board [part_number=BH1750FVI]
  Part2 = BH1750FVI Breakout Board [part_number=BH1750FVI]

nets:
  N1: VCC1.-, VCC2.+
  N2: VCC1.+, U1.TRIM, Q1.E, M2.pin_2, Q2.E, Q2.C
  N3: VCC2.-, U1.PGOOD, M1.pin_2, M2.pin_1
  GND: U1.ON_OFF, U1.SENSE, MBED1.GND, MBED1.Vin, Part1.GND, Part2.GND
  N4: Q1.B, MBED1.pin23
  N5: Q1.C, M1.pin_1
  N6: MBED1.pin9, Part1.SDA, Part2.SDA
  N7: MBED1.pin10, Part1.SCL, Part2.SCL
  N8: MBED1.pin22, Q2.B
  VCC: MBED1.VOUT, Part1.VCC, Part2.ADD, Part2.VCC

custom parts:
  BH1750FVI Breakout Board: The ROHM Semiconductor BH1750FVI is a digital ambient light sensor for the I2C bus interface. The BH750FVI is able to detect a wide range of light intensities (1-65535 lux). The spectral range is similar to that of the human eye.
